# Fritzing sketch AirsoftBomb (saved by Fritzing 0.9.3b)

parts:
  Arduino_Mega_2560 = Arduino Mega 2560 (Rev3)
  LCD_1602 = LCD screen
  S1 = Round Pushbutton
  S2 = Round Pushbutton
  U1 = LIPO-2000mAh [package=lipo-2000]
  S4 = Taiway 100-SP-X-T1 SPDT Miniature Toggle Switch [part_number=100-SP-X-T1-0-0-B1-M1 package=THT]
  S5 = Taiway 100-SP-X-T1 SPDT Miniature Toggle Switch [part_number=100-SP-X-T1-0-0-B1-M1 package=THT]
  J1 = Piezo Speaker
  Matrix_keypad1 = KEYPAD 4x4  # not connected
  U2 = POT [package=pot_alpha_rv16af-20]

nets:
  5V: Arduino_Mega_2560.5V, LCD_1602.VDD, S4.COM, S5.L1, U2.A
  GND: Arduino_Mega_2560.GND, LCD_1602.VSS, S1.leg0, S2.leg0, U1.-, J1.pin1, U2.E
  N1: Arduino_Mega_2560.D2_PWM, J1.pin2
  N2: Arduino_Mega_2560.D52, S2.leg1
  N3: Arduino_Mega_2560.D53, S1.leg1
  N4: LCD_1602.V0, U2.S
  N5: U1.+, S5.COM

custom parts:
  KEYPAD 4x4: Matrix keypad 16 buttons, 4 rows x 4 columns
